# Fritzing sketch CircuitoElectronico (saved by Fritzing 0.9.3b)
breadboards: 1

parts:
  Grove1 = Grove OLED 128x96
  Grove2 = Grove OLED 128x96
  Componente1 = Arduino Mega 2560 (Rev3)
  J1 = Basic Servo
  J2 = Basic Servo
  J3 = Basic Servo
  J4 = Basic Servo

nets:
  GND: Grove1.GND, Grove2.GND, Componente1.GND, J1.gnd, J2.gnd, J3.gnd, J4.gnd
  VCC: Grove1.VCC, Grove2.VCC, Componente1.5V, J1.vcc, J2.vcc, J3.vcc, J4.vcc
  N1: Grove1.SDA, Componente1.A4
  N2: Grove1.SCL, Componente1.A5
  N3: Grove2.SDA, Componente1.A9
  N4: Grove2.SCL, Componente1.A8
  N5: Componente1.D13_PWM, J1.pulse
  N6: Componente1.D12_PWM, J2.pulse
  N7: Componente1.D11_PWM, J3.pulse
  N8: Componente1.D10_PWM, J4.pulse
